// Digital circuit dram1.dig as structural Verilog
module dram1 (
  input  [3:0] Address_bit,
  input  clk,
  input  Input_Data,
  input  Store_Load,
  output [3:0] Output_Data
);

  wire and_1_out, and_2_out, and_3_out, and_4_out, and_5_out, and_6_out, and_7_out, and_8_out, and_9_out,
       and_10_out, and_11_out, and_12_out, and_14_out, and_15_out, and_16_out, decoder_1_out_0,
       decoder_1_out_1, decoder_1_out_2, decoder_1_out_3, decoder_1_out_4, decoder_1_out_5, decoder_1_out_6,
       decoder_1_out_7, decoder_1_out_8, decoder_1_out_9, decoder_1_out_10, decoder_1_out_11,
       decoder_1_out_12, decoder_1_out_13, decoder_1_out_14, decoder_1_out_15;
  wire [3:0] register_1_p4, register_2_p4, register_3_p4, register_4_p4, register_5_p4, register_6_p4,
       register_7_p4, register_8_p4, register_9_p4, register_10_p4, register_11_p4, register_12_p4,
       register_13_p2, register_14_p4, register_15_p4, register_16_p4;

  Decoder #(.Selector_Bits(4)) decoder_1 (
    .sel(Address_bit), .out_0(decoder_1_out_0), .out_1(decoder_1_out_1), .out_2(decoder_1_out_2),
    .out_3(decoder_1_out_3), .out_4(decoder_1_out_4), .out_5(decoder_1_out_5), .out_6(decoder_1_out_6),
    .out_7(decoder_1_out_7), .out_8(decoder_1_out_8), .out_9(decoder_1_out_9), .out_10(decoder_1_out_10),
    .out_11(decoder_1_out_11), .out_12(decoder_1_out_12), .out_13(decoder_1_out_13),
    .out_14(decoder_1_out_14), .out_15(decoder_1_out_15));
  and and_1 (and_1_out, decoder_1_out_0, clk);
  and and_2 (and_2_out, decoder_1_out_4, Input_Data);
  and and_3 (and_3_out, decoder_1_out_8, clk);
  and and_4 (and_4_out, decoder_1_out_12, clk);
  Multiplexer #(.Bits(4), .Selector_Bits(4)) multiplexer_1 (
    .sel(Address_bit), .in_0(register_1_p4), .in_1(register_5_p4), .in_2(register_9_p4),
    .in_3(register_13_p2), .in_4(register_2_p4), .in_5(register_6_p4), .in_6(register_10_p4),
    .in_7(register_14_p4), .in_8(register_3_p4), .in_9(register_7_p4), .in_10(register_11_p4),
    .in_11(register_15_p4), .in_12(register_4_p4), .in_13(register_8_p4), .in_14(register_12_p4),
    .in_15(register_16_p4), .out(Output_Data));
  // register register_1: pin names not known; wires that end beside it: and_1_out, Input_Data, Store_Load, register_1_p4
  // register register_2: pin names not known; wires that end beside it: and_2_out, Input_Data, Store_Load, register_2_p4
  // register register_3: pin names not known; wires that end beside it: and_3_out, Input_Data, Store_Load, register_3_p4
  // register register_4: pin names not known; wires that end beside it: and_4_out, Input_Data, Store_Load, register_4_p4
  and and_5 (and_5_out, decoder_1_out_1, Input_Data);
  and and_6 (and_6_out, decoder_1_out_5, clk);
  and and_7 (and_7_out, decoder_1_out_9, clk);
  and and_8 (and_8_out, decoder_1_out_13, clk);
  // register register_5: pin names not known; wires that end beside it: and_5_out, Input_Data, Store_Load, register_5_p4
  // register register_6: pin names not known; wires that end beside it: and_6_out, Input_Data, Store_Load, register_6_p4
  // register register_7: pin names not known; wires that end beside it: and_7_out, Input_Data, Store_Load, register_7_p4
  // register register_8: pin names not known; wires that end beside it: and_8_out, Input_Data, Store_Load, register_8_p4
  and and_9 (and_9_out, decoder_1_out_2, Input_Data);
  and and_10 (and_10_out, decoder_1_out_6, clk);
  and and_11 (and_11_out, decoder_1_out_10, clk);
  and and_12 (and_12_out, decoder_1_out_14, clk);
  // register register_9: pin names not known; wires that end beside it: and_9_out, Input_Data, Store_Load, register_9_p4
  // register register_10: pin names not known; wires that end beside it: and_10_out, Input_Data, Store_Load, register_10_p4
  // register register_11: pin names not known; wires that end beside it: and_11_out, Input_Data, Store_Load, register_11_p4
  // register register_12: pin names not known; wires that end beside it: and_12_out, Input_Data, Store_Load, register_12_p4
  and and_13 (Input_Data, decoder_1_out_3, Input_Data);
  and and_14 (and_14_out, decoder_1_out_7, clk);
  and and_15 (and_15_out, decoder_1_out_11, clk);
  and and_16 (and_16_out, decoder_1_out_15, clk);
  // register register_13: pin names not known; wires that end beside it: Store_Load, register_13_p2
  // register register_14: pin names not known; wires that end beside it: Input_Data, Store_Load, and_14_out, register_14_p4
  // register register_15: pin names not known; wires that end beside it: and_15_out, Input_Data, Store_Load, register_15_p4
  // register register_16: pin names not known; wires that end beside it: and_16_out, Input_Data, Store_Load, register_16_p4
endmodule
